# Fritzing sketch Untitled Sketch 3 (saved by Fritzing 0.9.4)
breadboards: 1

parts:
  S1 = Pushbutton [package="[THT]"]
  S2 = Pushbutton [package="[THT]"]
  S3 = Pushbutton [package="[THT]"]
  S4 = Pushbutton [package="[THT]"]
  S5 = Pushbutton [package="[THT]"]
  S6 = Pushbutton [package="[THT]"]
  R1 = Resistor [tolerance=±5% resistance=1k package=THT]
  R2 = Resistor [tolerance=±5% resistance=1k package=THT]
  R3 = Resistor [tolerance=±5% resistance=1k package=THT]
  R4 = Resistor [tolerance=±5% resistance=1k package=THT]
  R5 = Resistor [tolerance=±5% resistance=1k package=THT]
  R6 = Resistor [tolerance=±5% resistance=1k package=THT]
  Parça1 = Arduino Nano (Rev3.0)
  S7 = Pushbutton [package="[THT]"]
  R7 = Resistor [tolerance=±5% resistance=1k package=THT]
  LED1 = LEDs [package=led10mm]
  R8 = Resistor [tolerance=±5% resistance=10 package=THT]
  BAT2 = Battery Holders [package=lipo-1100mAh]
  S8 = Pushbutton [package="[THT]"]
  R9 = Resistor [tolerance=±5% resistance=1k package=THT]
  IR1 = TSOP312.., 314.. [package=THT]
  S9 = Pushbutton [package="[THT]"]
  R10 = Resistor [tolerance=±5% resistance=1k package=THT]
  S10 = SPST Switch [package=switche-dpdt]

nets:
  N1: S1.Pin_1, S1.Pin_2, S2.Pin_1, S2.Pin_2, S3.Pin_1, S3.Pin_2, S4.Pin_1, S4.Pin_2, S5.Pin_1, S5.Pin_2, S6.Pin_1, S6.Pin_2, S7.Pin_1, S7.Pin_2, S8.Pin_1, S8.Pin_2, IR1.Data, S9.Pin_1, S9.Pin_2
  N2: S1.Pin_3, S1.Pin_4, R1.Pin_0, Parça1.D8
  N3: S2.Pin_3, S2.Pin_4, R2.Pin_0
  N4: S3.Pin_3, S3.Pin_4, R3.Pin_0
  N5: S4.Pin_3, S4.Pin_4, R4.Pin_0
  N6: S5.Pin_3, S5.Pin_4, R5.Pin_0, Parça1.D4, Parça1.D5
  N7: S6.Pin_3, S6.Pin_4, R6.Pin_0
  N8: R1.Pin_1, R2.Pin_1, R3.Pin_1, R4.Pin_1, R5.Pin_1, R6.Pin_1, R7.Pin_1, LED1.C, IR1.Vs
  N9: Parça1.5V, S10.O
  N10: S7.Pin_3, S7.Pin_4, R7.Pin_0
  N11: LED1.LED_ŞERİT, R8.Pin_0
  N12: BAT2.+, S10.P
  N13: S8.Pin_3, S8.Pin_4, R9.Pin_0
  N14: S9.Pin_3, S9.Pin_4, R10.Pin_0

notes:
  - +
  IR LED
  1838 IR

custom parts:
  LEDs: LEDs Standard schematic elements and footprints for 5mm, 3mm, 1206, and 0603 sized LEDs. 5mm - Spark Fun Electronics SKU : COM-00529 (and others)
